# Fritzing sketch Scheme (saved by Fritzing 0.9.5d)
breadboards: 1

parts:
  Компонент1 = Arduino Nano (Rev3.0)
  J2 = Basic Servo
  R1 = Rotary Potentiometer (Small) [maximum_resistance=100kΩ package=THT]
  Power_5_5x2_1 = Power 5.5x2.5
  J3 = Basic Servo

nets:
  GND: Компонент1.GND, J2.gnd, R1.leg1, Power_5_5x2_1.GND, J3.gnd
  N1: Компонент1.D5, J3.pulse
  N2: Компонент1.D6, J2.pulse
  N3: Компонент1.5V, R1.leg2
  N4: Компонент1.A5, R1.wiper
  VCC: J2.vcc, Power_5_5x2_1.PWR, J3.vcc
